# Fritzing sketch Circuit 2 (saved by Fritzing 0.8.7b)
breadboards: 1

parts:
  Part1 = Arduino Uno (Rev3)
  R1 = PHOTOCELL [package=photocell-kit]
  LED1 = LED - 5mm [color="Red (633nm)" package="5 mm [THT]"]
  R4 = Resistor [tolerance=±5% resistance=220 package=THT]
  R5 = Resistor [tolerance=±5% resistance=10k package=THT]

nets:
  N1: Part1.A0, R1.P$2, R5.Pin_0
  N2: Part1.D13/SCK, R4.Pin_0
  N3: Part1.5V, R1.P$1
  N4: Part1.GND, LED1.cathode, R5.Pin_1
  N5: LED1.anode, R4.Pin_1
