# Fritzing sketch Circuit 3 (saved by Fritzing 0.8.7b)
breadboards: 1

parts:
  Part1 = Arduino Uno (Rev3)
  R1 = PHOTOCELL [package=photocell-kit]
  R5 = Resistor [tolerance=±5% resistance=10k package=THT]
  J1 = Basic Servo

nets:
  N1: Part1.A0, R1.P$2, R5.Pin_0
  N2: Part1.D9_PWM, J1.pulse
  5V: Part1.5V, R1.P$1, J1.vcc
  GND: Part1.GND, R5.Pin_1, J1.gnd
