# Fritzing sketch Circuit 5 (saved by Fritzing 0.8.7b)
breadboards: 1

parts:
  Part1 = Arduino Uno (Rev3)
  Part2 = SRF05 Ultrasonic Rangefinder

nets:
  N1: Part1.D10_PWM/SS, Part2.Trig
  N2: Part1.D11_PWM/MOSI, Part2.Echo
  5V: Part1.5V, Part2.VCC
  GND: Part1.GND, Part2.GND
