# Fritzing sketch Circuit 4 (saved by Fritzing 0.8.7b)
breadboards: 1

parts:
  Part1 = Arduino Uno (Rev3)
  R1 = PHOTOCELL [package=photocell-kit]
  R5 = Resistor [tolerance=±5% resistance=10k package=THT]
  J1 = Basic Servo
  Part3 = SRF05 Ultrasonic Rangefinder

nets:
  N1: Part1.A0, R1.P$2, R5.Pin_0
  N2: Part1.D9_PWM, J1.pulse
  N3: Part1.D10_PWM/SS, Part3.Trig
  N4: Part1.D11_PWM/MOSI, Part3.Echo
  VCC: Part1.5V, R1.P$1, J1.vcc, Part3.VCC
  GND: Part1.GND, R5.Pin_1, J1.gnd, Part3.GND
